# Fritzing sketch ARDUINO NANO W BUZZER (saved by Fritzing 0.9.5d)
breadboards: 1

parts:
  Part1 = Arduino Nano (Rev3.0)
  Mod1 = ESP32 - CAM

nets:
  N1: Part1.D1/TX, Mod1.VOT
  N2: Part1.D0/RX, Mod1.VOR
  GND: Part1.GND, Mod1.GND, Mod1.IO0
  5V: Part1.5V, Mod1.5V

custom parts:
  ESP32 - CAM: The ESP32-CAM has a very competitive small-size camera module that can operate independently as a minimum system with a footprint of only 27*40.5*4.5mm and a deep sleep current of up to 6mA.
